# Fritzing sketch zspod (saved by Fritzing 0.9.3b)
circuit board: 7.51224cm x 5.03909cm
breadboards: 1

parts:
  Arduino = Arduino Nano (Rev3.0)
  D23 = Diode [package=sma-diode]
  D28 = Diode [package=sma-diode]
  D22 = Diode [package=sma-diode]
  D24 = Diode [package=sma-diode]
  D25 = Diode [package=sma-diode]
  D26 = Diode [package=sma-diode]
  D27 = Diode [package=sma-diode]
  D29 = Diode [package=sma-diode]
  D30 = Diode [package=sma-diode]
  D31 = Diode [package=sma-diode]
  RTC = mystery part, 7 pins [chip_label=?]
  R4 = Resistor [tolerance=±5% resistance=100 package="0402 [SMD]"]
  R2 = Resistor [tolerance=±5% resistance=100 package="0402 [SMD]"]
  R1 = Resistor [tolerance=±5% resistance=100 package="0402 [SMD]"]
  R5 = Resistor [tolerance=±5% resistance=100 package="0402 [SMD]"]
  R6 = Resistor [tolerance=±5% resistance=100 package="0402 [SMD]"]
  R12 = Resistor [tolerance=±5% resistance=100 package="0402 [SMD]"]
  R8 = Resistor [tolerance=±5% resistance=100 package="0402 [SMD]"]
  R7 = Resistor [tolerance=±5% resistance=100 package="0402 [SMD]"]
  R9 = Resistor [tolerance=±5% resistance=100 package="0402 [SMD]"]
  R10 = Resistor [tolerance=±5% resistance=100 package="0402 [SMD]"]
  R11 = Resistor [tolerance=±5% resistance=100 package="0402 [SMD]"]
  h- = Momentary Switch [package=ksa_sealed_tac_switch]
  h+ = Momentary Switch [package=ksa_sealed_tac_switch]
  m- = Momentary Switch [package=ksa_sealed_tac_switch]
  m+ = Momentary Switch [package=ksa_sealed_tac_switch]
  D- = Momentary Switch [package=ksa_sealed_tac_switch]
  D+ = Momentary Switch [package=ksa_sealed_tac_switch]
  M- = Momentary Switch [package=ksa_sealed_tac_switch]
  M+ = Momentary Switch [package=ksa_sealed_tac_switch]
  Y- = Momentary Switch [package=ksa_sealed_tac_switch]
  RST = Momentary Switch [package=ksa_sealed_tac_switch]
  Y+ = Momentary Switch [package=ksa_sealed_tac_switch]
  BAT = mystery part, 2 pins [chip_label=?]
  EPD = EPD connector [package=sod-323]

nets:
  N1: Arduino.RESET, RST.1
  GND: Arduino.GND, RTC.pin6, R4.Pin_1, R2.Pin_1, R1.Pin_1, R5.Pin_1, R6.Pin_1, R12.Pin_1, R8.Pin_1, R7.Pin_1, R9.Pin_1, R10.Pin_1, R11.Pin_1, RST.3, BAT.pin2, EPD.GND
  N2: Arduino.D2, D23.C, D28.C, D22.C, D24.C, D25.C, D26.C, D27.C, D29.C, D30.C, D31.C, R12.Pin_0
  N3: Arduino.D3, RTC.pin1
  N4: Arduino.D4, D30.A, R10.Pin_0, h+.1, h+.2
  N5: Arduino.D5, D29.A, R9.Pin_0, m-.1, m-.2
  N6: Arduino.D6, D28.A, R8.Pin_0, m+.1, m+.2
  N7: Arduino.D7, EPD.BUSY
  N8: Arduino.D8, EPD.RST
  N9: Arduino.D9, EPD.DC
  N10: Arduino.D10, EPD.CS
  N11: Arduino.D11/MOSI, EPD.DIN
  N12: Arduino.D12/MISO, D31.A, R11.Pin_0, h-.1, h-.2
  5V: Arduino.5V, RTC.pin5, h-.3, h-.4, h+.3, h+.4, m-.3, m-.4, m+.3, m+.4, D-.3, D-.4, D+.3, D+.4, M-.3, M-.4, M+.3, M+.4, Y-.3, Y-.4, Y+.3, Y+.4, BAT.pin1, EPD.VCC
  N13: Arduino.A7, D27.A, R7.Pin_0, D-.1, D-.2
  N14: Arduino.A6, D26.A, R6.Pin_0, D+.1, D+.2
  N15: Arduino.A5, RTC.pin3
  N16: Arduino.A4, RTC.pin4
  N17: Arduino.A3, D25.A, R5.Pin_0, M-.1, M-.2
  N18: Arduino.A2, D24.A, R4.Pin_0, M+.1, M+.2
  N19: Arduino.A1, D23.A, R2.Pin_0, Y-.1, Y-.2
  N20: Arduino.A0, D22.A, R1.Pin_0, Y+.1, Y+.2
  N21: Arduino.D13/SCK, EPD.CLK

notes:
  +
  -
  zspod
  h
  m
  D
  M
  Y
  RST
  SQ
  VCC

// code stored in the sketch: zspod.ino
#include <Wire.h>
#include <RTClib.h>
#include <avr/sleep.h>
#include <avr/power.h>

#include <SPI.h>
#include "epd4in2.h"
#include "epdpaint.h"

#include "buttons.h"
#include "trans.h"
#include "timing.h"
#include "globals.h"

#define COLORED     0
#define UNCOLORED   1

#define TOPBAR_HEIGHT 30
#define BIGSTRING_MARGIN 5
#define BIGSTRING_SINGLE_Y ((300 - TOPBAR_HEIGHT - FONT60_HEIGHT) / 2  + TOPBAR_HEIGHT)
#define BIGSTRING_DOUBLE_Y_UPPER ((300 - TOPBAR_HEIGHT - (FONT60_HEIGHT * 2) - BIGSTRING_MARGIN ) / 2 + TOPBAR_HEIGHT)
#define BIGSTRING_DOUBLE_Y_LOWER (BIGSTRING_DOUBLE_Y_UPPER + FONT60_HEIGHT + BIGSTRING_MARGIN)
 
#define SMALLSTRING_X (400 - 17 * 5) / 2
#define SMALLSTRING_Y (300 - TOPBAR_HEIGHT - 24) / 2 + TOPBAR_HEIGHT


unsigned char image[750];
Paint paint(image, 200, 30);
Epd epd;

char text_1[20] = {0};
char text_2[20] = {0};

void setup() {
  // RTC and serial
  Serial.begin(9600);
  rtc.begin();

  DateTime now = rtc.now();
  Serial.print("Start time: ");
  char dt_format[] = DATE_TIME_FORMAT;
  Serial.println(now.toString(dt_format));

  // buttons
  init_buttons();

  // display
  updateDisplay();
  
  // Timing
  Timer::init_timer();
  delay(100); 
}


void loop() {
  int secs_to_sleep = time_change_mode ? 5 : secsToSleep();
  time_change_mode = false;
  Timer::start_timer(secs_to_sleep);
  Timer::do_sleep();
  updateDisplay();
}

void  updateDisplay() {
  
  DateTime now = rtc.now();
  //now = DateTime(2021, 12, 12, 11, 29, 0);

  char dateTemplate[] = ", DD.MM.YYYY";
  char date[30];
  const char* weekday = Trans::weekdays[now.dayOfTheWeek()];
  strcpy(date, weekday);
  strcpy(date + strlen(weekday), now.toString(dateTemplate));

  char timecode[6];
  char t_format[] = TIME_FORMAT;
  strcpy(timecode, now.toString(t_format));

  char dt_format[] = DATE_TIME_FORMAT;
  Serial.print("Refresh Time: ");
  Serial.println(now.toString(dt_format));

  // (400 - strlen(date)* fontwidth) / 2
  int fromLeft = 200 - (strlen(date) * 17) / 2;

  epd.Init();
  epd.ClearFrameHidden();

  paint.SetHeight(TOPBAR_HEIGHT);
  paint.SetWidth(200);
  paint.Clear(UNCOLORED);
  paint.DrawFilledRectangle(0,0, 200, TOPBAR_HEIGHT, COLORED);
  paint.DrawStringAt(fromLeft, 5, date, &Font24, UNCOLORED);
  paint.DrawStringAt(100, 100, timecode, &Font24, COLORED);
  epd.SetPartialWindow(paint.GetImage(), 0, 0, paint.GetWidth(), paint.GetHeight());
  
  paint.Clear(UNCOLORED);
  paint.DrawFilledRectangle(0, 0, 200, TOPBAR_HEIGHT, COLORED);
  paint.DrawStringAt(fromLeft - 200, 5, date, &Font24, UNCOLORED);
  epd.SetPartialWindow(paint.GetImage(), 200, 0, paint.GetWidth(), paint.GetHeight());


  if (!time_change_mode) {
    Trans::upperString(now, text_1);
    Trans::lowerString(now, text_2);
  
    int width_upper = paint.BigStringWidth(text_1, font60);
    int width_lower = paint.BigStringWidth(text_2, font60);
  
    int from_left_upper = 200 - width_upper / 2;
    int from_left_lower = 200 - width_lower / 2;
    
    paint.DrawBigStringAt(from_left_upper, BIGSTRING_DOUBLE_Y_UPPER, text_1, font60, COLORED, epd);
    paint.DrawBigStringAt(from_left_lower, width_upper ? BIGSTRING_DOUBLE_Y_LOWER : BIGSTRING_SINGLE_Y, text_2, font60, COLORED, epd);
  }
  else {
    paint.Clear(UNCOLORED);
    paint.DrawStringAt(0, 0, timecode, &Font24, COLORED);
    epd.SetPartialWindow(paint.GetImage(), SMALLSTRING_X, SMALLSTRING_Y, paint.GetWidth(), paint.GetHeight());
  }

  epd.DisplayFrame();
  epd.Sleep();

  // wait for flush
  delay(50);
}

int secsToSleep() {
  DateTime now = rtc.now();
  
  uint8_t mins = now.minute();
  int next_wakeup_mins = Trans::roundTo(mins, 5) + 3;

  int secs_til_wake = (next_wakeup_mins - mins) * 60 - now.second() + 3;

  return secs_til_wake;
}
